// Digital circuit CPU.dig as structural Verilog
module CPU (
  input  [7:0] value,
  input  [1:0] dest,
  input  [1:0] src,
  input  tworeg,
  output [31:0] r0,
  output [31:0] r1,
  output [31:0] r2,
  output [31:0] r3,
  output [1:0] rd,
  output [1:0] rd_2,
  output [31:0] L,
  output [1:0] rs,
  output [31:0] target,
  output [3:0] PC,
  output [31:0] R,
  output [1:0] rd_3,
  output [1:0] rs_2,
  output [31:0] R_2
);

  wire add, add_out, Advance_out, assembler_1_p9, assembler_1_p10, decoder_1_p1, decoder_1_p2,
       fecthc_counter_1_p7, jump, jump_out, mode_out, move, move_out, pm_1_p6, pm_1_p7, pm_1_p8;
  wire [1:0] decoder_1_p11;
  wire [3:0] pm_1_p4;
  wire [15:0] pm_1_p5, PROGRAM_d;
  wire [31:0] execute_1_result;

  LED programming (.in(mode_out));
  DipSwitch mode (.out(mode_out));
  Button u_add (.out(add_out));
  Button u_move (.out(move_out));
  Button u_jump (.out(jump_out));
  // assembler assembler_1: pin names not known; wires that end beside it: mode_out, value, dest, src, tworeg, add_out, move_out, jump_out, assembler_1_p9, assembler_1_p10
  // PM pm_1: pin names not known; wires that end beside it: assembler_1_p9, assembler_1_p10, PC, pm_1_p4, pm_1_p5, pm_1_p6, pm_1_p7, pm_1_p8
  EEPROMDualPort #(.AddrBits(4), .Bits(16)) PROGRAM (
    .A(pm_1_p4), .Din(pm_1_p5), .str(pm_1_p6), .C(pm_1_p7), .ld(pm_1_p8), .D(PROGRAM_d));
  Button Advance (.out(Advance_out));
  // fecthc_counter fecthc_counter_1: pin names not known; wires that end beside it: mode_out, assembler_1_p9, PROGRAM_d, Advance_out, R, jump, fecthc_counter_1_p7, PC
  LED led_1 (.in(jump));
  LED led_2 (.in(add));
  LED led_3 (.in(move));
  // decoder decoder_1: pin names not known; wires that end beside it: decoder_1_p1, decoder_1_p2, fecthc_counter_1_p7, rs, rd, L, R, add, jump, move, decoder_1_p11
  execute execute_1 (.L(L), .R(R), .result_mux(decoder_1_p11), .result(execute_1_result));
  // reg_file reg_file_1: pin names not known; wires that end beside it: rs, rd, execute_1_result, Advance_out, decoder_1_p1, decoder_1_p2, r0, r1, r2, r3

  assign R_2 = R;
  assign rd_2 = rd;
  assign rd_3 = rd;
  assign rs_2 = rs;
  assign target = R;

  // Notes on the sheet:
  //   value: default 1
  //   dest: default 1
  //   src: default 1
  //   tworeg: default 1
  //   0. R2=R2+1
  //   1. R2=R1+R2
  //   2. R3=R2
  //   3. R1=R1+R2
  //   4. R3=R1
  //   5. JUMP 1
  //   contents of PROGRAM (hex, n*v repeats v):
  //   1a0,61,bd,91,10e,10e
  //   jump
  //   add
  //   move
  //   R
  //   pc =
  //   =
  //   (R               )
  //   +
endmodule
